// Logisim project CPU.circ as structural Verilog: 7 circuits, main circuit main
module main (
);

  wire [4:0] alu_1_carry, flagregister_1_flagsout;
  wire [15:0] n16buff_1_out, n16buff_2_out, regfile_1_out_9, regfile_1_read_1, undriven;

  _16Reg u_16reg_1 ();  // open: in_1, in_2, out_3
  RegFile regfile_1 (
    .out_9(regfile_1_out_9), .Read_1(regfile_1_read_1));  // open: Write_data, Clock, Reset, Read_select_1, Read_select_2, Write_enable, Write_select
  _16Buff u_16buff_1 (.In(regfile_1_read_1), .Out(n16buff_1_out));  // open: Enable
  _16Buff u_16buff_2 (.In(regfile_1_out_9), .Out(n16buff_2_out));  // open: Enable
  _16Buff u_16buff_3 (.In(undriven), .Out(n16buff_2_out));  // open: Enable
  ALU alu_1 (
    .A(n16buff_1_out), .B(n16buff_2_out), .Carry(alu_1_carry[0]), .Flag(alu_1_carry[1]),
    .Low(alu_1_carry[2]), .Negative(alu_1_carry[3]), .Zero(alu_1_carry[4]));  // open: OpCode, CarryIn, C
  FlagRegister flagregister_1 (.FlagsIn(alu_1_carry), .FlagsOut(flagregister_1_flagsout));  // open: Clock
endmodule

module RegFile (
  input  Reset,
  input  [3:0] Read_select_1,
  input  Write_enable,
  input  [3:0] Write_select,
  input  [15:0] Write_data,
  input  [3:0] Read_select_2,
  input  Clock,
  output [15:0] Read_1,
  output [15:0] out_9
);
endmodule

module ALU (
  input  [15:0] A,
  input  [15:0] B,
  input  [7:0] OpCode,
  input  CarryIn,
  output [15:0] C,
  output Carry,
  output Flag,
  output Low,
  output Negative,
  output Zero
);
endmodule

module _16Buff (
  input  [15:0] In,
  input  Enable,
  output [15:0] Out
);
endmodule

module _18Buff (
  input  [15:0] In,
  input  Enable,
  output [15:0] Out
);
endmodule

module FlagRegister (
  input  [4:0] FlagsIn,
  input  Clock,
  output [4:0] FlagsOut
);
endmodule

module _16Reg (
  input  [15:0] in_1,
  input  in_2,
  output [15:0] out_3
);
endmodule
